// Logisim project CRC.circ as structural Verilog: 3 circuits, main circuit CRC
module CRC (
  input  [7:0] in_1,
  input  [3:0] divisor,
  output [10:0] out_3
);

  wire [3:0] n4_bit_crc_1_out_4, n4_bit_crc_2_out_4, n4_bit_crc_3_out_4, n4_bit_crc_4_out_4,
       n4_bit_crc_5_out_4, n4_bit_crc_6_out_4, n4_bit_crc_7_out_4;

  _4_bit_CRC u_4_bit_crc_1 (.dividend(in_1[7:4]), .number(in_1[3]), .divisor(divisor), .out_4(n4_bit_crc_1_out_4));
  _4_bit_CRC u_4_bit_crc_2 (
    .dividend(n4_bit_crc_1_out_4), .number(in_1[2]), .divisor(divisor), .out_4(n4_bit_crc_2_out_4));
  _4_bit_CRC u_4_bit_crc_3 (
    .dividend(n4_bit_crc_2_out_4), .number(in_1[1]), .divisor(divisor), .out_4(n4_bit_crc_3_out_4));
  _4_bit_CRC u_4_bit_crc_4 (
    .dividend(n4_bit_crc_3_out_4), .number(in_1[0]), .divisor(divisor), .out_4(n4_bit_crc_4_out_4));
  _4_bit_CRC u_4_bit_crc_5 (
    .dividend(n4_bit_crc_4_out_4), .number(1'b0), .divisor(divisor), .out_4(n4_bit_crc_5_out_4));
  _4_bit_CRC u_4_bit_crc_6 (
    .dividend(n4_bit_crc_5_out_4), .number(1'b0), .divisor(divisor), .out_4(n4_bit_crc_6_out_4));
  _4_bit_CRC u_4_bit_crc_7 (
    .dividend(n4_bit_crc_6_out_4), .number(1'b0), .divisor(divisor), .out_4(n4_bit_crc_7_out_4));
  _4_bit_end u_4_bit_end_1 (.dividend(n4_bit_crc_7_out_4), .divisor(divisor), .out_3(out_3[2:0]));

  assign out_3[10:3] = in_1;

  // Notes on the sheet:
  //   dividend
endmodule

module _4_bit_CRC (
  input  [3:0] dividend,
  input  number,
  input  [3:0] divisor,
  output [3:0] out_4
);

  wire comparator_1_lt, select;
  wire [3:0] xor_1_out;
  wire [3:3] multiplexer_1_out;

  Comparator #(.width(4), .mode("unsigned")) comparator_1 (
    .a(dividend), .b(4'b1000), .lt(comparator_1_lt));  // open: gt, eq
  not not_1 (select, comparator_1_lt);
  assign xor_1_out = dividend ^ divisor;  // XOR_Gate xor_1, 4 bits wide
  Multiplexer #(.width(4)) multiplexer_1 (
    .in0(dividend), .in1(xor_1_out), .out({multiplexer_1_out[3], out_4[3:1]}), .sel(select));  // open: en

  assign out_4[0] = number;
endmodule

module _4_bit_end (
  input  [3:0] dividend,
  input  [3:0] divisor,
  output [2:0] out_3
);

  wire comparator_1_lt, select;
  wire [3:0] xor_1_out;
  wire [3:3] multiplexer_1_out;

  Comparator #(.width(4), .mode("unsigned")) comparator_1 (
    .a(dividend), .b(4'b1000), .lt(comparator_1_lt));  // open: gt, eq
  not not_1 (select, comparator_1_lt);
  assign xor_1_out = dividend ^ divisor;  // XOR_Gate xor_1, 4 bits wide
  Multiplexer #(.width(4)) multiplexer_1 (
    .in0(dividend), .in1(xor_1_out), .out({multiplexer_1_out[3], out_3}), .sel(select));  // open: en
endmodule
