// Logisim project fsm.circ as structural Verilog: 3 circuits, main circuit fsm
module fsm (
  input  CLR,
  input  [1:0] In,
  output Z
);

  wire clock_1_out;
  wire [2:0] and_1_out, bit_extender_1_out, not_1_out, register_1_q, state_change_1_s_0o;

  assign bit_extender_1_out = {{2{CLR}}, CLR};  // Bit_Extender bit_extender_1
  state_change state_change_1 (
    .In_1(In[1]), .In_0(In[0]), .s_2(register_1_q[2]), .s_1(register_1_q[1]), .s_0(register_1_q[0]),
    .s_2o(state_change_1_s_0o[2]), .s_1o(state_change_1_s_0o[1]), .s_0o(state_change_1_s_0o[0]));
  Clock clock_1 (.out(clock_1_out));
  assign not_1_out = ~bit_extender_1_out;  // NOT_Gate not_1, 3 bits wide
  assign and_1_out = not_1_out & state_change_1_s_0o;  // AND_Gate and_1, 3 bits wide
  Register #(.width(3)) register_1 (.D(and_1_out), .Q(register_1_q), .clk(clock_1_out));  // open: en, clr
  \output  output_1 (.In_0(In[0]), .s_2(register_1_q[2]), .s_1(register_1_q[1]), .s_0(register_1_q[0]), .Z(Z));

  // Other names for the same wires on the sheet: In_0 = In[0]; In_1 = In[1]
endmodule

module state_change (
  input  In_1,
  input  In_0,
  input  s_2,
  input  s_1,
  input  s_0,
  output s_2o,
  output s_1o,
  output s_0o
);

  wire and_1_out, and_2_out, and_3_out, and_4_out, and_5_out, and_6_out, and_7_out, and_8_out, and_9_out,
       not_1_out, not_2_out, not_3_out, not_4_out, not_5_out, not_6_out, not_7_out, not_8_out, not_9_out,
       not_10_out, not_11_out, not_12_out, not_13_out, not_14_out, not_15_out, not_16_out, not_17_out,
       not_18_out, not_19_out, not_20_out, not_21_out, not_22_out;

  not not_1 (not_1_out, In_0);
  not not_2 (not_2_out, s_2);
  not not_3 (not_3_out, s_1);
  not not_4 (not_4_out, In_0);
  not not_5 (not_5_out, s_0);
  not not_6 (not_6_out, In_0);
  not not_7 (not_7_out, s_0);
  not not_8 (not_8_out, In_1);
  not not_9 (not_9_out, In_0);
  not not_10 (not_10_out, s_2);
  not not_11 (not_11_out, s_1);
  not not_12 (not_12_out, In_1);
  not not_13 (not_13_out, In_0);
  not not_14 (not_14_out, s_0);
  not not_15 (not_15_out, In_1);
  not not_16 (not_16_out, In_0);
  not not_17 (not_17_out, s_0);
  not not_18 (not_18_out, In_0);
  not not_19 (not_19_out, s_0);
  not not_20 (not_20_out, In_0);
  not not_21 (not_21_out, s_0);
  not not_22 (not_22_out, In_1);
  and and_1 (and_1_out, In_1, not_1_out, not_2_out, not_3_out, s_0);
  and and_2 (and_2_out, In_1, not_4_out, s_1, not_5_out);
  and and_3 (and_3_out, In_1, not_6_out, s_2, not_7_out);
  and and_4 (and_4_out, not_8_out, not_9_out, not_10_out, not_11_out, s_0);
  and and_5 (and_5_out, not_12_out, not_13_out, s_1, not_14_out);
  and and_6 (and_6_out, not_15_out, not_16_out, s_2, not_17_out);
  and and_7 (and_7_out, not_18_out, s_1, not_19_out);
  and and_8 (and_8_out, not_20_out, s_2, not_21_out);
  and and_9 (and_9_out, not_22_out, In_0);
  or or_1 (s_2o, and_1_out, and_2_out, and_3_out);
  or or_2 (s_1o, and_4_out, and_5_out, and_6_out);
  or or_3 (s_0o, and_7_out, and_8_out, and_9_out);
endmodule

module \output  (
  input  In_0,
  input  s_2,
  input  s_1,
  input  s_0,
  output Z
);

  wire and_1_out, and_2_out, and_3_out, not_1_out, not_2_out, not_3_out, not_4_out;

  not not_1 (not_1_out, In_0);
  not not_2 (not_2_out, s_0);
  not not_3 (not_3_out, In_0);
  not not_4 (not_4_out, s_0);
  and and_1 (and_1_out, not_1_out, s_1, not_2_out);
  and and_2 (and_2_out, not_3_out, s_2, not_4_out);
  and and_3 (and_3_out, s_2, s_1);
  or or_1 (Z, and_1_out, and_2_out, and_3_out);
endmodule
