// Logisim project ftoi.circ as structural Verilog: 3 circuits, main circuit ftoi
module ftoi (
  input  [15:0] S,
  output [31:0] out_2
);

  wire comparator_1_eq, comparator_2_lt, judge;
  wire [4:0] subtractor_1_out, subtractor_2_out, subtractor_3_out;
  wire [31:0] bit_extender_1_out, calculate_1_out_3, multiplexer_1_out, multiplexer_2_out, multiplier_1_out,
       shifter_1_out;

  judge judge_1 (.S(S[14:10]), .out_2(judge));
  Subtractor #(.width(5)) subtractor_1 (.a(S[14:10]), .b(5'b01111), .out(subtractor_1_out));  // open: bin, bout
  Comparator #(.width(1), .mode("unsigned")) comparator_1 (.a(S[15]), .b(1'b1), .eq(comparator_1_eq));  // open: gt, lt
  Subtractor #(.width(5)) subtractor_2 (.a(5'b01010), .b(subtractor_1_out), .out(subtractor_2_out));  // open: bin, bout
  Subtractor #(.width(5)) subtractor_3 (.a(subtractor_1_out), .b(5'b01010), .out(subtractor_3_out));  // open: bin, bout
  Comparator #(.width(5), .mode("unsigned")) comparator_2 (
    .a(subtractor_1_out), .b(5'b01010), .lt(comparator_2_lt));  // open: gt, eq
  assign bit_extender_1_out = {{21{1'b0}}, {1'b1, S[9:0]}};  // Bit_Extender bit_extender_1
  calculate calculate_1 (.in_1({1'b1, S[9:0]}), .in_2(subtractor_2_out), .out_3(calculate_1_out_3));
  Shifter #(.width(32)) shifter_1 (.in(bit_extender_1_out), .\dist (subtractor_3_out), .out(shifter_1_out));
  Multiplexer #(.width(32)) multiplexer_1 (
    .in0(shifter_1_out), .in1(calculate_1_out_3), .out(multiplexer_1_out), .sel(comparator_2_lt));  // open: en
  Multiplexer #(.width(32)) multiplexer_2 (
    .in0(multiplexer_1_out), .in1(multiplier_1_out), .out(multiplexer_2_out), .sel(comparator_1_eq));  // open: en
  Multiplier #(.width(32)) multiplier_1 (
    .a(multiplexer_1_out), .b({32{1'b1}}), .out(multiplier_1_out));  // open: cin, cout
  Multiplexer #(.width(32)) multiplexer_3 (
    .in0(multiplexer_2_out), .in1({32{1'b0}}), .out(out_2), .sel(judge));  // open: en

  // Notes on the sheet:
  //   M
  //   1+10 bit
  //   E
endmodule

module judge (
  input  [4:0] S,
  output out_2
);

  wire comparator_1_eq, comparator_2_lt;

  Comparator #(.width(5), .mode("unsigned")) comparator_1 (.a(S), .b({5{1'b1}}), .eq(comparator_1_eq));  // open: gt, lt
  Comparator #(.width(5), .mode("unsigned")) comparator_2 (.a(S), .b(5'b01111), .lt(comparator_2_lt));  // open: gt, eq
  or or_1 (out_2, comparator_1_eq, comparator_2_lt);
endmodule

module calculate (
  input  [10:0] in_1,
  input  [4:0] in_2,
  output [31:0] out_3
);

  wire [3:0] bit_extender_1_out;
  wire [10:0] shifter_1_out;

  Bit_Extender #(.in_width(5), .out_width(4)) bit_extender_1 (.in(in_2), .out(bit_extender_1_out));
  Shifter #(.width(11), .shift("lr")) shifter_1 (.in(in_1), .\dist (bit_extender_1_out), .out(shifter_1_out));
  assign out_3 = {{21{1'b0}}, shifter_1_out};  // Bit_Extender bit_extender_2
endmodule
