// Logisim project grf.circ as structural Verilog: 3 circuits, main circuit grf
module grf (
  input  in_1,
  input  in_2,
  input  WE,
  input  [4:0] in_4,
  input  [4:0] in_5,
  input  [4:0] in_6,
  input  [31:0] in_7,
  output [31:0] out_8,
  output [31:0] out_9
);

  wire _1, _2, _3, _4, _5, _6, _7, _8, _9, _10, _11, _12, _13, _14, _15, _16, _17, _18, _19, _20, _21, _22,
       _23, _24, _25, _26, _27, _28, _29, _30, _31, _32;
  wire [31:0] _1_minus, _2_minus, _3_minus, _4_minus, _5_minus, _6_minus, _7_minus, _8_minus, _9_minus,
       _10_minus, _11_minus, _12_minus, _13_minus, _14_minus, _15_minus, _16_minus, _17_minus, _18_minus,
       _19_minus, _20_minus, _21_minus, _22_minus, _23_minus, _24_minus, _25_minus, _26_minus, _27_minus,
       _28_minus, _29_minus, _30_minus, _31_minus, _32_minus;

  grf_8_0 grf_8_0_1 (
    .WE(_1), .in_2(_2), .in_3(_3), .in_4(_4), .in_5(_5), .in_6(_6), .CLK(in_1), .in_8(_7), .reset(in_2),
    .in_10(_8), .in_11(in_7), .out_12(_1_minus), .out_13(_2_minus), .out_14(_3_minus), .out_15(_4_minus),
    .out_16(_5_minus), .out_17(_6_minus), .out_18(_7_minus), .out_19(_8_minus));
  grf_8 grf_8_1 (
    .WE(_9), .in_2(_10), .in_3(_11), .in_4(_12), .in_5(_13), .in_6(_14), .CLK(in_1), .in_8(_15),
    .reset(in_2), .in_10(_16), .in_11(in_7), .out_12(_9_minus), .out_13(_10_minus), .out_14(_11_minus),
    .out_15(_12_minus), .out_16(_13_minus), .out_17(_14_minus), .out_18(_15_minus), .out_19(_16_minus));
  grf_8 grf_8_2 (
    .WE(_17), .in_2(_18), .in_3(_19), .in_4(_20), .in_5(_21), .in_6(_22), .CLK(in_1), .in_8(_23),
    .reset(in_2), .in_10(_24), .in_11(in_7), .out_12(_17_minus), .out_13(_18_minus), .out_14(_19_minus),
    .out_15(_20_minus), .out_16(_21_minus), .out_17(_22_minus), .out_18(_23_minus), .out_19(_24_minus));
  Demultiplexer #(.select(5)) demultiplexer_1 (
    .out0(_1), .out1(_2), .out2(_3), .out3(_4), .out4(_5), .out5(_6), .out6(_7), .out7(_8), .out8(_9),
    .out9(_10), .out10(_11), .out11(_12), .out12(_13), .out13(_14), .out14(_15), .out15(_16), .out16(_17),
    .out17(_18), .out18(_19), .out19(_20), .out20(_21), .out21(_22), .out22(_23), .out23(_24), .out24(_25),
    .out25(_26), .out26(_27), .out27(_28), .out28(_29), .out29(_30), .out30(_31), .out31(_32), .in(WE),
    .sel(in_6));  // open: en
  grf_8 grf_8_3 (
    .WE(_25), .in_2(_26), .in_3(_27), .in_4(_28), .in_5(_29), .in_6(_30), .CLK(in_1), .in_8(_31),
    .reset(in_2), .in_10(_32), .in_11(in_7), .out_12(_25_minus), .out_13(_26_minus), .out_14(_27_minus),
    .out_15(_28_minus), .out_16(_29_minus), .out_17(_30_minus), .out_18(_31_minus), .out_19(_32_minus));
  Multiplexer #(.select(5), .width(32)) multiplexer_1 (
    .in0(_1_minus), .in1(_2_minus), .in2(_3_minus), .in3(_4_minus), .in4(_5_minus), .in5(_6_minus),
    .in6(_7_minus), .in7(_8_minus), .in8(_9_minus), .in9(_10_minus), .in10(_11_minus), .in11(_12_minus),
    .in12(_13_minus), .in13(_14_minus), .in14(_15_minus), .in15(_16_minus), .in16(_17_minus),
    .in17(_18_minus), .in18(_19_minus), .in19(_20_minus), .in20(_21_minus), .in21(_22_minus),
    .in22(_23_minus), .in23(_24_minus), .in24(_25_minus), .in25(_26_minus), .in26(_27_minus),
    .in27(_28_minus), .in28(_29_minus), .in29(_30_minus), .in30(_31_minus), .in31(_32_minus), .out(out_9),
    .sel(in_5));  // open: en
  Multiplexer #(.select(5), .width(32)) multiplexer_2 (
    .in0(_1_minus), .in1(_2_minus), .in2(_3_minus), .in3(_4_minus), .in4(_5_minus), .in5(_6_minus),
    .in6(_7_minus), .in7(_8_minus), .in8(_9_minus), .in9(_10_minus), .in10(_11_minus), .in11(_12_minus),
    .in12(_13_minus), .in13(_14_minus), .in14(_15_minus), .in15(_16_minus), .in16(_17_minus),
    .in17(_18_minus), .in18(_19_minus), .in19(_20_minus), .in20(_21_minus), .in21(_22_minus),
    .in22(_23_minus), .in23(_24_minus), .in24(_25_minus), .in25(_26_minus), .in26(_27_minus),
    .in27(_28_minus), .in28(_29_minus), .in29(_30_minus), .in30(_31_minus), .in31(_32_minus), .out(out_8),
    .sel(in_4));  // open: en

  // Other names for the same wires on the sheet: A1[4:0] = in_4; A2[4:0] = in_5; A3[4:0] = in_6; reset = in_2

  // Notes on the sheet:
  //   WD
  //   RD1
  //   RD2
endmodule

module grf_8 (
  input  WE,
  input  in_2,
  input  in_3,
  input  in_4,
  input  in_5,
  input  in_6,
  input  CLK,
  input  in_8,
  input  reset,
  input  in_10,
  input  [31:0] in_11,
  output [31:0] out_12,
  output [31:0] out_13,
  output [31:0] out_14,
  output [31:0] out_15,
  output [31:0] out_16,
  output [31:0] out_17,
  output [31:0] out_18,
  output [31:0] out_19
);

  Register #(.width(32)) register_1 (.D(in_11), .en(WE), .Q(out_12), .clk(CLK), .clr(reset));
  Register #(.width(32)) register_2 (.D(in_11), .en(in_2), .Q(out_13), .clk(CLK), .clr(reset));
  Register #(.width(32)) register_3 (.D(in_11), .en(in_3), .Q(out_14), .clk(CLK), .clr(reset));
  Register #(.width(32)) register_4 (.D(in_11), .en(in_4), .Q(out_15), .clk(CLK), .clr(reset));
  Register #(.width(32)) register_5 (.D(in_11), .en(in_5), .Q(out_16), .clk(CLK), .clr(reset));
  Register #(.width(32)) register_6 (.D(in_11), .en(in_6), .Q(out_17), .clk(CLK), .clr(reset));
  Register #(.width(32)) register_7 (.D(in_11), .en(in_8), .Q(out_18), .clk(CLK), .clr(reset));
  Register #(.width(32)) register_8 (.D(in_11), .en(in_10), .Q(out_19), .clk(CLK), .clr(reset));

  // Other names for the same wires on the sheet: _1 = WE; _1_out[31:0] = out_12; _2 = in_2; _2_out[31:0] = out_13;
  //   _3 = in_3; _3_out[31:0] = out_14; _4 = in_4; _4_out[31:0] = out_15; _5 = in_5; _5_out[31:0] = out_16; _6 = in_6;
  //   _6_out[31:0] = out_17; _7 = in_8; _7_out[31:0] = out_18; _8 = in_10; _8_out[31:0] = out_19

  // Notes on the sheet:
  //   WE
endmodule

module grf_8_0 (
  input  WE,
  input  in_2,
  input  in_3,
  input  in_4,
  input  in_5,
  input  in_6,
  input  CLK,
  input  in_8,
  input  reset,
  input  in_10,
  input  [31:0] in_11,
  output [31:0] out_12,
  output [31:0] out_13,
  output [31:0] out_14,
  output [31:0] out_15,
  output [31:0] out_16,
  output [31:0] out_17,
  output [31:0] out_18,
  output [31:0] out_19
);

  wire [31:0] register_1_q;

  Register #(.width(32)) register_1 (.D(in_11), .en(WE), .Q(register_1_q), .clk(CLK), .clr(reset));
  Register #(.width(32)) register_2 (.D(in_11), .en(in_3), .Q(out_14), .clk(CLK), .clr(reset));
  Register #(.width(32)) register_3 (.D(in_11), .en(in_2), .Q(out_13), .clk(CLK), .clr(reset));
  Register #(.width(32)) register_4 (.D(in_11), .en(in_4), .Q(out_15), .clk(CLK), .clr(reset));
  Register #(.width(32)) register_5 (.D(in_11), .en(in_5), .Q(out_16), .clk(CLK), .clr(reset));
  Register #(.width(32)) register_6 (.D(in_11), .en(in_6), .Q(out_17), .clk(CLK), .clr(reset));
  Register #(.width(32)) register_7 (.D(in_11), .en(in_8), .Q(out_18), .clk(CLK), .clr(reset));
  Register #(.width(32)) register_8 (.D(in_11), .en(in_10), .Q(out_19), .clk(CLK), .clr(reset));

  assign out_12 = {32{1'b0}};
  // also tied to GND on the sheet: {register_1_q[0], register_1_q[1], register_1_q[2], register_1_q[3], register_1_q[4], register_1_q[5], register_1_q[6], register_1_q[7], register_1_q[8], register_1_q[9], register_1_q[10], register_1_q[11], register_1_q[12], register_1_q[13], register_1_q[14], register_1_q[15], register_1_q[16], register_1_q[17], register_1_q[18], register_1_q[19], register_1_q[20], register_1_q[21], register_1_q[22], register_1_q[23], register_1_q[24], register_1_q[25], register_1_q[26], register_1_q[27], register_1_q[28], register_1_q[29], register_1_q[30], register_1_q[31]}

  // Other names for the same wires on the sheet: _1 = WE; _2 = in_2; _2_out[31:0] = out_13; _3 = in_3;
  //   _3_out[31:0] = out_14; _4 = in_4; _4_out[31:0] = out_15; _5 = in_5; _5_out[31:0] = out_16; _6 = in_6;
  //   _6_out[31:0] = out_17; _7 = in_8; _7_out[31:0] = out_18; _8 = in_10; _8_out[31:0] = out_19

  // Notes on the sheet:
  //   WE
endmodule
