// Logisim project navigation.circ as structural Verilog: 3 circuits, main circuit navigation
module navigation (
  input  [1:0] dir,
  input  clk,
  input  reset,
  output out_4,
  output out_5
);

  wire [3:0] register_1_q, state_change_1_s_0o;

  state_change state_change_1 (
    .dir_1(dir[1]), .dir_0(dir[0]), .s_3o(state_change_1_s_0o[3]), .s_3(register_1_q[3]),
    .s_2(register_1_q[2]), .s_1(register_1_q[1]), .s_0(register_1_q[0]), .s_2o(state_change_1_s_0o[2]),
    .s_1o(state_change_1_s_0o[1]), .s_0o(state_change_1_s_0o[0]));
  Register #(.width(4)) register_1 (.D(state_change_1_s_0o), .Q(register_1_q), .clk(clk), .clr(reset));  // open: en
  state_output state_output_1 (.s_3(register_1_q[3]), .s_0(register_1_q[0]), .arrive(out_4), .hit(out_5));

  // Other names for the same wires on the sheet: dir_0 = dir[0]; dir_1 = dir[1]
endmodule

module state_change (
  input  dir_1,
  input  dir_0,
  input  s_3,
  input  s_2,
  input  s_1,
  input  s_0,
  output s_3o,
  output s_2o,
  output s_1o,
  output s_0o
);

  wire and_1_out, and_2_out, and_3_out, and_4_out, and_5_out, and_6_out, and_7_out, and_8_out, and_9_out,
       and_10_out, and_11_out, and_12_out, and_13_out, and_14_out, and_15_out, and_16_out, and_17_out,
       and_18_out, and_19_out, and_20_out, not_1_out, not_2_out, not_3_out, not_4_out, not_5_out, not_6_out,
       not_7_out, not_8_out, not_9_out, not_10_out, not_11_out, not_12_out, not_13_out, not_14_out,
       not_15_out, not_16_out, not_17_out, not_18_out, not_19_out, not_20_out, not_21_out, not_22_out,
       not_23_out, not_24_out, not_25_out, not_26_out, not_27_out, not_28_out, not_29_out, not_30_out,
       not_31_out, not_32_out, not_33_out;

  not not_1 (not_1_out, dir_1);
  not not_2 (not_2_out, dir_0);
  not not_3 (not_3_out, s_0);
  not not_4 (not_4_out, dir_1);
  not not_5 (not_5_out, s_1);
  not not_6 (not_6_out, dir_1);
  not not_7 (not_7_out, s_2);
  not not_8 (not_8_out, dir_1);
  not not_9 (not_9_out, dir_0);
  not not_10 (not_10_out, s_1);
  not not_11 (not_11_out, dir_1);
  not not_12 (not_12_out, dir_0);
  not not_13 (not_13_out, s_1);
  not not_14 (not_14_out, dir_1);
  not not_15 (not_15_out, dir_0);
  not not_16 (not_16_out, s_3);
  not not_17 (not_17_out, s_2);
  not not_18 (not_18_out, s_1);
  not not_19 (not_19_out, dir_1);
  not not_20 (not_20_out, dir_0);
  not not_21 (not_21_out, dir_0);
  not not_22 (not_22_out, dir_1);
  not not_23 (not_23_out, dir_0);
  not not_24 (not_24_out, s_1);
  not not_25 (not_25_out, s_0);
  not not_26 (not_26_out, s_2);
  not not_27 (not_27_out, s_1);
  not not_28 (not_28_out, dir_1);
  not not_29 (not_29_out, s_2);
  not not_30 (not_30_out, s_1);
  not not_31 (not_31_out, dir_0);
  not not_32 (not_32_out, s_2);
  not not_33 (not_33_out, s_1);
  and and_1 (and_1_out, not_1_out, not_2_out, s_2, s_1);
  and and_2 (and_2_out, s_3, not_3_out);
  and and_3 (and_3_out, not_4_out, dir_0, s_2, not_5_out);
  and and_4 (and_4_out, not_6_out, not_7_out, s_1);
  and and_5 (and_5_out, not_8_out, not_9_out, s_2, not_10_out);
  and and_6 (and_6_out, not_11_out, dir_0, s_1);
  and and_7 (and_7_out, dir_1, not_12_out, s_2, s_1);
  and and_8 (and_8_out, dir_1, dir_0, s_2, not_13_out);
  and and_9 (and_9_out, not_14_out, not_15_out, not_16_out, not_17_out, not_18_out);
  and and_10 (and_10_out, not_19_out, not_20_out, s_3, s_0);
  and and_11 (and_11_out, dir_0, s_1);
  and and_12 (and_12_out, dir_1, not_21_out, s_2);
  and and_13 (and_13_out, not_22_out, not_23_out, s_2, not_24_out);
  and and_14 (and_14_out, s_3, not_25_out);
  and and_15 (and_15_out, dir_0, not_26_out, not_27_out);
  and and_16 (and_16_out, not_28_out, dir_0, s_2, s_1);
  and and_17 (and_17_out, dir_1, not_29_out, not_30_out);
  and and_18 (and_18_out, dir_1, not_31_out, s_2, s_1);
  and and_19 (and_19_out, dir_1, dir_0, not_32_out);
  and and_20 (and_20_out, dir_1, dir_0, not_33_out);
  or or_1 (s_3o, and_1_out, and_2_out, and_3_out);
  or or_2 (s_2o, and_4_out, and_5_out, and_6_out, and_7_out, and_8_out);
  or or_3 (s_1o, and_9_out, and_10_out, and_11_out, and_12_out);
  or or_4 (s_0o, and_13_out, and_14_out, and_15_out, and_16_out, and_17_out, and_18_out, and_19_out, and_20_out);
endmodule

module state_output (
  input  s_3,
  input  s_0,
  output arrive,
  output hit
);

  wire not_1_out, not_2_out;

  and and_1 (arrive, s_3, not_1_out);
  not not_1 (not_1_out, s_0);
  not not_2 (not_2_out, s_3);
  and and_2 (hit, not_2_out, s_0);
endmodule
