// Logisim project CPU.circ as structural Verilog: 7 circuits, main circuit main
module main (
  input  in_1,
  output [31:0] Instr,
  output GRFWr,
  output [4:0] A3,
  output [31:0] RegWD,
  output DMWr,
  output [4:0] A,
  output [31:0] MemWD
);

  wire BSel, CLK, EXTOp, Zero;
  wire [1:0] A3Sel, ALUOp, NPCOp, WDSel;
  wire [15:0] Imm16;
  wire [31:0] A_t, D, Ext, Imm32, imm32_t, multiplexer_3_out, PC4, RD1;

  Clock clock_1 (.out(CLK));
  IFU ifu_1 (.Reset(in_1), .Zero(Zero), .Instr(Instr), .imm16(Imm16), .CLK(CLK), .NPCOp(NPCOp), .PC4(PC4), .RA(RD1));
  EXT ext_1 (.imm16(Imm16), .Ext(imm32_t), .EXTOp(EXTOp), .imm32(Ext));
  Multiplexer #(.select(2), .width(5)) multiplexer_1 (
    .in0(Instr[15:11]), .in1(Instr[20:16]), .in2({5{1'b1}}), .out(A3), .sel(A3Sel));  // open: in3, en
  Multiplexer #(.select(2), .width(32)) multiplexer_2 (
    .in0({A_t[31:7], A, A_t[1:0]}), .in1(D), .in2(PC4), .in3(Imm32), .out(RegWD), .sel(WDSel));  // open: en
  Controller controller_1 (
    .funct(Instr[5:0]), .opcode(Instr[31:26]), .NPCOp(NPCOp), .GRFWr(GRFWr), .EXTOp(EXTOp), .ALUOp(ALUOp),
    .DMWr(DMWr), .A3Sel(A3Sel), .WDSel(WDSel), .BSel(BSel));
  GRF grf_1 (
    .CLK(CLK), .Reset(in_1), .RFWr(GRFWr), .A1(Instr[25:21]), .A2(Instr[20:16]), .A3(A3), .WD(RegWD),
    .RD1(RD1), .RD2(MemWD));
  ALU alu_1 (.A(RD1), .B(multiplexer_3_out), .C({A_t[31:7], A, A_t[1:0]}), .Zero(Zero), .ALUOp(ALUOp));
  Multiplexer #(.width(32)) multiplexer_3 (.in0(MemWD), .in1(Ext), .out(multiplexer_3_out), .sel(BSel));  // open: en
  DM dm_1 (.CLK(CLK), .Reset(in_1), .DMWr(DMWr), .A({A_t[31:7], A, A_t[1:0]}), .WD(MemWD), .RD(D));

  // Other names for the same wires on the sheet: C[31:0] = {A_t[31:7], A, A_t[1:0]}; A_t[6:2] = A;
  //   funct[5:0] = Instr[5:0]; rd[4:0] = Instr[15:11]; rt[4:0] = Instr[20:16]; rs[4:0] = Instr[25:21];
  //   opcode[5:0] = Instr[31:26]; RD2[31:0] = MemWD; Reset = in_1
endmodule

module GRF (
  input  CLK,
  input  Reset,
  input  RFWr,
  input  [4:0] A1,
  input  [4:0] A2,
  input  [4:0] A3,
  input  [31:0] WD,
  output [31:0] RD1,
  output [31:0] RD2
);

  wire _1, _2, _3, _4, _5, _6, _7, _8, _9, _10, _11, _12, _13, _14, _15, _16, _17, _18, _19, _20, _21, _22,
       _23, _24, _25, _26, _27, _28, _29, _30, _31;
  wire [31:0] _1_minus, _2_minus, _3_minus, _4_minus, _5_minus, _6_minus, _7_minus, _8_minus, _9_minus,
       _10_minus, _11_minus, _12_minus, _13_minus, _14_minus, _15_minus, _16_minus, _17_minus, _18_minus,
       _19_minus, _20_minus, _21_minus, _22_minus, _23_minus, _24_minus, _25_minus, _26_minus, _27_minus,
       _28_minus, _29_minus, _30_minus, _31_minus;

  Demultiplexer #(.select(5)) demultiplexer_1 (
    .out1(_1), .out2(_2), .out3(_3), .out4(_4), .out5(_5), .out6(_6), .out7(_7), .out8(_8), .out9(_9),
    .out10(_10), .out11(_11), .out12(_12), .out13(_13), .out14(_14), .out15(_15), .out16(_16), .out17(_17),
    .out18(_18), .out19(_19), .out20(_20), .out21(_21), .out22(_22), .out23(_23), .out24(_24), .out25(_25),
    .out26(_26), .out27(_27), .out28(_28), .out29(_29), .out30(_30), .out31(_31), .in(RFWr), .sel(A3));  // open: out0, en
  Register #(.width(32)) u__8 (.D(WD), .en(_8), .Q(_8_minus), .clk(CLK), .clr(Reset));
  Register #(.width(32)) u__16 (.D(WD), .en(_16), .Q(_16_minus), .clk(CLK), .clr(Reset));
  Register #(.width(32)) u__24 (.D(WD), .en(_24), .Q(_24_minus), .clk(CLK), .clr(Reset));
  Register #(.width(32)) u__1 (.D(WD), .en(_1), .Q(_1_minus), .clk(CLK), .clr(Reset));
  Register #(.width(32)) u__9 (.D(WD), .en(_9), .Q(_9_minus), .clk(CLK), .clr(Reset));
  Register #(.width(32)) u__17 (.D(WD), .en(_17), .Q(_17_minus), .clk(CLK), .clr(Reset));
  Register #(.width(32)) u__25 (.D(WD), .en(_25), .Q(_25_minus), .clk(CLK), .clr(Reset));
  Register #(.width(32)) u__2 (.D(WD), .en(_2), .Q(_2_minus), .clk(CLK), .clr(Reset));
  Register #(.width(32)) u__10 (.D(WD), .en(_10), .Q(_10_minus), .clk(CLK), .clr(Reset));
  Register #(.width(32)) u__18 (.D(WD), .en(_18), .Q(_18_minus), .clk(CLK), .clr(Reset));
  Register #(.width(32)) u__26 (.D(WD), .en(_26), .Q(_26_minus), .clk(CLK), .clr(Reset));
  Register #(.width(32)) u__3 (.D(WD), .en(_3), .Q(_3_minus), .clk(CLK), .clr(Reset));
  Register #(.width(32)) u__11 (.D(WD), .en(_11), .Q(_11_minus), .clk(CLK), .clr(Reset));
  Register #(.width(32)) u__19 (.D(WD), .en(_19), .Q(_19_minus), .clk(CLK), .clr(Reset));
  Register #(.width(32)) u__27 (.D(WD), .en(_27), .Q(_27_minus), .clk(CLK), .clr(Reset));
  Register #(.width(32)) u__4 (.D(WD), .en(_4), .Q(_4_minus), .clk(CLK), .clr(Reset));
  Register #(.width(32)) u__12 (.D(WD), .en(_12), .Q(_12_minus), .clk(CLK), .clr(Reset));
  Register #(.width(32)) u__20 (.D(WD), .en(_20), .Q(_20_minus), .clk(CLK), .clr(Reset));
  Register #(.width(32)) u__28 (.D(WD), .en(_28), .Q(_28_minus), .clk(CLK), .clr(Reset));
  Register #(.width(32)) u__5 (.D(WD), .en(_5), .Q(_5_minus), .clk(CLK), .clr(Reset));
  Register #(.width(32)) u__13 (.D(WD), .en(_13), .Q(_13_minus), .clk(CLK), .clr(Reset));
  Register #(.width(32)) u__21 (.D(WD), .en(_21), .Q(_21_minus), .clk(CLK), .clr(Reset));
  Register #(.width(32)) u__29 (.D(WD), .en(_29), .Q(_29_minus), .clk(CLK), .clr(Reset));
  Register #(.width(32)) u__6 (.D(WD), .en(_6), .Q(_6_minus), .clk(CLK), .clr(Reset));
  Register #(.width(32)) u__14 (.D(WD), .en(_14), .Q(_14_minus), .clk(CLK), .clr(Reset));
  Register #(.width(32)) u__22 (.D(WD), .en(_22), .Q(_22_minus), .clk(CLK), .clr(Reset));
  Register #(.width(32)) u__23 (.D(WD), .en(_23), .Q(_23_minus), .clk(CLK), .clr(Reset));
  Register #(.width(32)) u__31 (.D(WD), .en(_31), .Q(_31_minus), .clk(CLK), .clr(Reset));
  Register #(.width(32)) u__30 (.D(WD), .en(_30), .Q(_30_minus), .clk(CLK), .clr(Reset));
  Register #(.width(32)) u__7 (.D(WD), .en(_7), .Q(_7_minus), .clk(CLK), .clr(Reset));
  Register #(.width(32)) u__15 (.D(WD), .en(_15), .Q(_15_minus), .clk(CLK), .clr(Reset));
  Multiplexer #(.select(5), .width(32)) multiplexer_1 (
    .in0({32{1'b0}}), .in1(_1_minus), .in2(_2_minus), .in3(_3_minus), .in4(_4_minus), .in5(_5_minus),
    .in6(_6_minus), .in7(_7_minus), .in8(_8_minus), .in9(_9_minus), .in10(_10_minus), .in11(_11_minus),
    .in12(_12_minus), .in13(_13_minus), .in14(_14_minus), .in15(_15_minus), .in16(_16_minus),
    .in17(_17_minus), .in18(_18_minus), .in19(_19_minus), .in20(_20_minus), .in21(_21_minus),
    .in22(_22_minus), .in23(_23_minus), .in24(_24_minus), .in25(_25_minus), .in26(_26_minus),
    .in27(_27_minus), .in28(_28_minus), .in29(_29_minus), .in30(_30_minus), .in31(_31_minus), .out(RD1),
    .sel(A1));  // open: en
  Multiplexer #(.select(5), .width(32)) multiplexer_2 (
    .in0({32{1'b0}}), .in1(_1_minus), .in2(_2_minus), .in3(_3_minus), .in4(_4_minus), .in5(_5_minus),
    .in6(_6_minus), .in7(_7_minus), .in8(_8_minus), .in9(_9_minus), .in10(_10_minus), .in11(_11_minus),
    .in12(_12_minus), .in13(_13_minus), .in14(_14_minus), .in15(_15_minus), .in16(_16_minus),
    .in17(_17_minus), .in18(_18_minus), .in19(_19_minus), .in20(_20_minus), .in21(_21_minus),
    .in22(_22_minus), .in23(_23_minus), .in24(_24_minus), .in25(_25_minus), .in26(_26_minus),
    .in27(_27_minus), .in28(_28_minus), .in29(_29_minus), .in30(_30_minus), .in31(_31_minus), .out(RD2),
    .sel(A2));  // open: en

  // Other names for the same wires on the sheet: Wr = RFWr

  // Notes on the sheet:
  //   Wr
  //   Wr
  //   Wr
  //   Wr
  //   RD1
  //   RD2
endmodule

module ALU (
  input  [31:0] A,
  input  [31:0] B,
  input  [1:0] ALUOp,
  output [31:0] C,
  output Zero
);

  wire [31:0] adder_1_out, or_1_out, subtractor_1_out;

  Adder #(.width(32)) adder_1 (.a(A), .b(B), .out(adder_1_out));  // open: cin, cout
  Subtractor #(.width(32)) subtractor_1 (.a(A), .b(B), .out(subtractor_1_out));  // open: bin, bout
  assign or_1_out = A | B;  // OR_Gate or_1, 32 bits wide
  Multiplexer #(.select(2), .width(32)) multiplexer_1 (
    .in0(adder_1_out), .in1(subtractor_1_out), .in2(or_1_out), .out(C), .sel(ALUOp));  // open: in3, en
  Comparator #(.width(32), .mode("unsigned")) comparator_1 (.a(C), .b({32{1'b0}}), .eq(Zero));  // open: gt, lt

  // Notes on the sheet:
  //   addu
  //   subu
  //   or
  //   eq
endmodule

module DM (
  input  CLK,
  input  Reset,
  input  DMWr,
  input  [31:0] A,
  input  [31:0] WD,
  output [31:0] RD
);

  RAM #(.addrWidth(5), .dataWidth(32), .bus("separate")) ram_1 (
    .addr(A[6:2]), .din(WD), .data(RD), .str(DMWr), .clk(CLK), .clr(Reset));  // open: sel, ld

  // Other names for the same wires on the sheet: A_t[4:0] = A[6:2]
endmodule

module EXT (
  input  EXTOp,
  input  [15:0] imm16,
  output [31:0] Ext,
  output [31:0] imm32
);

  wire [31:0] bit_extender_1_out, bit_extender_2_out;

  assign bit_extender_1_out = {{16{1'b0}}, imm16};  // Bit_Extender bit_extender_1
  assign bit_extender_2_out = {{16{imm16[15]}}, imm16};  // Bit_Extender bit_extender_2
  Multiplexer #(.width(32)) multiplexer_1 (
    .in0(bit_extender_1_out), .in1(bit_extender_2_out), .out(Ext), .sel(EXTOp));  // open: en
endmodule

module Controller (
  input  [5:0] opcode,
  input  [5:0] funct,
  output [1:0] NPCOp,
  output GRFWr,
  output EXTOp,
  output [1:0] ALUOp,
  output DMWr,
  output [1:0] A3Sel,
  output [1:0] WDSel,
  output BSel
);

  wire addu, beq, jal, jr, lui, lw, not_1_out, not_2_out, not_3_out, not_4_out, not_5_out, not_6_out,
       not_7_out, not_8_out, not_9_out, not_10_out, not_11_out, not_12_out, ori, Rtype, subu, sw;

  not not_1 (not_1_out, opcode[5]);
  not not_2 (not_2_out, opcode[4]);
  not not_3 (not_3_out, opcode[3]);
  not not_4 (not_4_out, opcode[2]);
  not not_5 (not_5_out, opcode[1]);
  not not_6 (not_6_out, opcode[0]);
  not not_7 (not_7_out, funct[5]);
  not not_8 (not_8_out, funct[4]);
  not not_9 (not_9_out, funct[3]);
  not not_10 (not_10_out, funct[2]);
  not not_11 (not_11_out, funct[1]);
  not not_12 (not_12_out, funct[0]);
  and and_1 (Rtype, not_1_out, not_2_out, not_3_out, not_4_out, not_5_out, not_6_out);
  and and_2 (addu, funct[5], not_8_out, not_9_out, Rtype, not_10_out, not_11_out, funct[0]);
  and and_3 (ori, not_1_out, not_2_out, opcode[3], opcode[2], not_5_out, opcode[0]);
  and and_4 (subu, funct[5], not_8_out, not_9_out, Rtype, not_10_out, funct[1], funct[0]);
  or or_1 (NPCOp[0], beq, jr);
  or or_2 (NPCOp[1], jal, jr);
  or or_3 (GRFWr, ori, addu, subu, lw, jal, lui);
  or or_4 (EXTOp, lw, sw);
  or or_5 (ALUOp[0], subu, beq);
  buf or_6 (ALUOp[1], ori);  // OR_Gate
  buf or_7 (DMWr, sw);  // OR_Gate
  or or_8 (A3Sel[0], ori, lw, lui);
  buf or_9 (A3Sel[1], jal);  // OR_Gate
  or or_10 (WDSel[0], lw, lui);
  or or_11 (WDSel[1], jal, lui);
  or or_12 (BSel, ori, lw, sw);
  and and_5 (lw, opcode[5], not_2_out, not_3_out, not_4_out, opcode[1], opcode[0]);
  and and_6 (jr, not_7_out, not_8_out, funct[3], Rtype, not_10_out, not_11_out, not_12_out);
  and and_7 (sw, opcode[5], not_2_out, opcode[3], not_4_out, opcode[1], opcode[0]);
  and and_8 (beq, not_1_out, not_2_out, not_3_out, opcode[2], not_5_out, not_6_out);
  and and_9 (jal, not_1_out, not_2_out, not_3_out, not_4_out, opcode[1], opcode[0]);
  and and_10 (lui, not_1_out, not_2_out, opcode[3], opcode[2], opcode[1], opcode[0]);

  // Other names for the same wires on the sheet: A3Sel_0 = A3Sel[0]; A3Sel_1 = A3Sel[1]; ALUOp_0 = ALUOp[0];
  //   ALUOp_1 = ALUOp[1]; funct_0 = funct[0]; funct_1 = funct[1]; funct_2 = funct[2]; funct_3 = funct[3];
  //   funct_4 = funct[4]; funct_5 = funct[5]; NPCOp_0 = NPCOp[0]; NPCOp_1 = NPCOp[1]; opcode_0 = opcode[0];
  //   opcode_1 = opcode[1]; opcode_2 = opcode[2]; opcode_3 = opcode[3]; opcode_4 = opcode[4]; opcode_5 = opcode[5];
  //   WDSel_0 = WDSel[0]; WDSel_1 = WDSel[1]
endmodule

module IFU (
  input  Reset,
  input  Zero,
  input  CLK,
  input  [1:0] NPCOp,
  input  [31:0] RA,
  output [31:0] Instr,
  output [31:0] PC4,
  output [15:0] imm16
);

  wire [31:0] adder_2_out, bit_extender_1_out, multiplexer_1_out, NPC, PC;

  Adder #(.width(32)) adder_1 (.a(PC), .b(32'h4), .out(PC4));  // open: cin, cout
  assign bit_extender_1_out = {{14{imm16[15]}}, {imm16, 2'b00}};  // Bit_Extender bit_extender_1
  Register #(.width(32)) u_PC (.D(NPC), .Q(PC), .clk(CLK), .clr(Reset));  // open: en
  Adder #(.width(32)) adder_2 (.a(PC4), .b(bit_extender_1_out), .out(adder_2_out));  // open: cin, cout
  Multiplexer #(.width(32)) multiplexer_1 (
    .in0(PC4), .in1(adder_2_out), .out(multiplexer_1_out), .sel(Zero));  // open: en
  Multiplexer #(.select(2), .width(32)) multiplexer_2 (
    .in0(PC4), .in1(multiplexer_1_out), .in2({PC[31:28], Instr[25:16], imm16, 2'b00}), .in3(RA), .out(NPC),
    .sel(NPCOp));  // open: en
  ROM #(.addrWidth(5), .dataWidth(32)) rom_1 (.addr(PC[6:2]), .data({Instr[31:16], imm16}));  // open: sel

  assign Instr[15:0] = imm16;

  // Other names for the same wires on the sheet: Imm[15:0] = imm16; instr_index[25:0] = {Instr[25:16], imm16};
  //   NPCOp_0 = NPCOp[0]; NPCOp_1 = NPCOp[1]
endmodule
